# Fritzing sketch circuit_scheme (saved by Fritzing 0.9.3b)
breadboards: 6

parts:
  Part1 = Arduino Uno (Rev3)
  U1 = 74HC595 [package="DIP16 [THT]"]
  U2 = 74HC595 [package="DIP16 [THT]"]
  U3 = 74HC595 [package="DIP16 [THT]"]
  U4 = 74HC595 [package="DIP16 [THT]"]
  IC1 = DS1307 [package=THT]
  R1 = Resistor [tolerance=±5% resistance=220 package=THT]
  R2 = Resistor [tolerance=±5% resistance=220 package=THT]
  R3 = Resistor [tolerance=±5% resistance=220 package=THT]
  R4 = Resistor [tolerance=±5% resistance=220 package=THT]
  R5 = Resistor [tolerance=±5% resistance=220 package=THT]
  R6 = Resistor [tolerance=±5% resistance=220 package=THT]
  R7 = Resistor [tolerance=±5% resistance=220 package=THT]
  R8 = Resistor [tolerance=±5% resistance=220 package=THT]
  LED1 = LED - 3mm [color="Red (633nm)" package="3 mm [THT]"]
  LED2 = LED - 3mm [color="Red (633nm)" package="3 mm [THT]"]
  LED3 = LED - 3mm [color="Red (633nm)" package="3 mm [THT]"]
  LED4 = LED - 3mm [color="Red (633nm)" package="3 mm [THT]"]
  LED5 = LED - 3mm [color="Red (633nm)" package="3 mm [THT]"]
  LED6 = LED - 3mm [color="Red (633nm)" package="3 mm [THT]"]
  LED7 = LED - 3mm [color="Red (633nm)" package="3 mm [THT]"]
  LED8 = LED - 3mm [color="Red (633nm)" package="3 mm [THT]"]
  R9 = Resistor [tolerance=±5% resistance=220 package=THT]
  R10 = Resistor [tolerance=±5% resistance=220 package=THT]
  R11 = Resistor [tolerance=±5% resistance=220 package=THT]
  R12 = Resistor [tolerance=±5% resistance=220 package=THT]
  R13 = Resistor [tolerance=±5% resistance=220 package=THT]
  R14 = Resistor [tolerance=±5% resistance=220 package=THT]
  R15 = Resistor [tolerance=±5% resistance=220 package=THT]
  R16 = Resistor [tolerance=±5% resistance=220 package=THT]
  LED9 = LED - 3mm [color="Red (633nm)" package="3 mm [THT]"]
  LED10 = LED - 3mm [color="Red (633nm)" package="3 mm [THT]"]
  LED11 = LED - 3mm [color="Red (633nm)" package="3 mm [THT]"]
  LED12 = LED - 3mm [color="Red (633nm)" package="3 mm [THT]"]
  LED13 = LED - 3mm [color="Red (633nm)" package="3 mm [THT]"]
  LED14 = LED - 3mm [color="Red (633nm)" package="3 mm [THT]"]
  LED15 = LED - 3mm [color="Red (633nm)" package="3 mm [THT]"]
  LED16 = LED - 3mm [color="Red (633nm)" package="3 mm [THT]"]

nets:
  N1: Part1.A4/SDA, IC1.SDA_-_I2C_Data
  N2: Part1.A5/SCL, IC1.SCL_-_I2C_Clock
  N3: Part1.D8, U1.ST_CP, U2.ST_CP
  N4: Part1.D11_PWM/MOSI, U1.DS
  N5: Part1.D12/MISO, U1.SH_CP, U2.SH_CP
  VCC: Part1.5V, U1.Q7', U1.MR, U1.VCC, U2.Q7', U2.VCC, IC1.+V
  GND: Part1.GND, U1.GND, U1.OE, U2.GND, U2.OE, IC1.0V, LED1.anode, LED2.anode, LED3.anode, LED4.anode, LED5.anode, LED6.anode, LED7.anode, LED8.anode, LED9.anode, LED10.anode, LED11.anode, LED12.anode, LED13.anode, LED14.anode, LED15.anode, LED16.anode
  N6: U1.Q1, R2.Pin_0
  N7: U1.Q2, R3.Pin_0
  N8: U1.Q3, R4.Pin_0
  N9: U1.Q4, R5.Pin_0
  N10: U1.Q5, R6.Pin_0
  N11: U1.Q6, R7.Pin_0
  N12: U1.Q7, R8.Pin_0
  N13: U1.Q0, R1.Pin_0
  N14: U2.Q1, R10.Pin_0
  N15: U2.Q2, R11.Pin_0
  N16: U2.Q3, R12.Pin_0
  N17: U2.Q4, R13.Pin_0
  N18: U2.Q5, R14.Pin_0
  N19: U2.Q6, R15.Pin_0
  N20: U2.Q7, R16.Pin_0
  N21: U2.Q0, R9.Pin_0
  GND_2: U3.GND, U4.GND
  N22: R1.Pin_1, LED1.cathode
  N23: R2.Pin_1, LED2.cathode
  N24: R3.Pin_1, LED3.cathode
  N25: R4.Pin_1, LED4.cathode
  N26: R5.Pin_1, LED5.cathode
  N27: R6.Pin_1, LED6.cathode
  N28: R7.Pin_1, LED7.cathode
  N29: R8.Pin_1, LED8.cathode
  N30: R9.Pin_1, LED9.cathode
  N31: R10.Pin_1, LED10.cathode
  N32: R11.Pin_1, LED11.cathode
  N33: R12.Pin_1, LED12.cathode
  N34: R13.Pin_1, LED13.cathode
  N35: R14.Pin_1, LED14.cathode
  N36: R15.Pin_1, LED15.cathode
  N37: R16.Pin_1, LED16.cathode

notes:
  Note 1: The actual RTC element used was DS1338. It was wired the same way - same pins on the element connected to the same pins on the Arduino
